// Logisim project SUB_TRY.circ as structural Verilog: 1 circuit, main circuit SUB_TRY
module SUB_TRY (
  input  A2,
  input  A1,
  input  A0,
  output z
);

  wire and_1_out, and_2_out, not_1_out, not_2_out;

  not not_1 (not_1_out, A2);
  not not_2 (not_2_out, A0);
  and and_1 (and_1_out, not_1_out, A0);
  and and_2 (and_2_out, A1, not_2_out);
  or or_1 (z, and_1_out, and_2_out);
endmodule
