// Logisim project Tunnels.circ as structural Verilog: 1 circuit, main circuit Tunnels
module Tunnels (
  input  in_1,
  input  in_2,
  input  in_3,
  input  in_4
);

  Hex_Digit_Display hex_digit_display_1 (.value({in_4, in_3, in_2, in_1}));  // open: dp

  // Other names for the same wires on the sheet: Bit_3 = in_1; Bit_2 = in_2; Bit_1 = in_3; Bit_0 = in_4
endmodule
