// Logisim project dispdemo.circ as structural Verilog: 1 circuit, main circuit dispdemo
module dispdemo (
  input  in_1,
  input  in_2,
  input  in_3,
  input  in_4
);

  Hex_Digit_Display hex_digit_display_1 (.value({in_1, in_2, in_3, in_4}));  // open: dp
endmodule
