// Logisim project kbddemo.circ as structural Verilog: 1 circuit, main circuit kbddemo
module kbddemo (
  input  [3:0] in_1,
  output out_2,
  output out_3,
  output out_4,
  output out_5
);


  assign out_2 = in_1[3];
  assign out_3 = in_1[2];
  assign out_4 = in_1[1];
  assign out_5 = in_1[0];
endmodule
