// Logisim project subdemo.circ as structural Verilog: 1 circuit, main circuit subdemo
module subdemo (
  input  in_1,
  input  in_2,
  input  in_3,
  output out_4
);

  SUB_TRY sub_try_1 (.A2(in_1), .A1(in_2), .A0(in_3), .z(out_4));
endmodule
